// Logisim project Memory-Project.circ as structural Verilog: 3 circuits, main circuit main
module main (
);

  wire clock_1_out;

  Clock clock_1 (.out(clock_1_out));
  D_Flip_Flop #(.trigger("falling")) d_ff_1 (.clk(clock_1_out));  // open: D, Q, Qn, preset, en, reset
  D_Flip_Flop #(.trigger("falling")) d_ff_2 ();  // open: clk, D, Q, Qn, preset, en, reset
  D_Flip_Flop #(.trigger("falling")) d_ff_3 ();  // open: clk, D, Q, Qn, preset, en, reset
  D_Flip_Flop #(.trigger("falling")) d_ff_4 ();  // open: clk, D, Q, Qn, preset, en, reset
  D_Flip_Flop #(.trigger("falling")) d_ff_5 ();  // open: clk, D, Q, Qn, preset, en, reset
  D_Flip_Flop #(.trigger("falling")) d_ff_6 ();  // open: clk, D, Q, Qn, preset, en, reset
  D_Flip_Flop #(.trigger("falling")) d_ff_7 ();  // open: clk, D, Q, Qn, preset, en, reset
  D_Flip_Flop #(.trigger("falling")) d_ff_8 ();  // open: clk, D, Q, Qn, preset, en, reset
  D_Flip_Flop #(.trigger("falling")) d_ff_9 ();  // open: clk, D, Q, Qn, preset, en, reset
  D_Flip_Flop #(.trigger("falling")) d_ff_10 ();  // open: clk, D, Q, Qn, preset, en, reset
  D_Flip_Flop #(.trigger("falling")) d_ff_11 ();  // open: clk, D, Q, Qn, preset, en, reset
  D_Flip_Flop #(.trigger("falling")) d_ff_12 ();  // open: clk, D, Q, Qn, preset, en, reset
endmodule

module _12_bit_Register (
  input  [11:0] D,
  input  Reset,
  input  Write,
  input  C,
  output [11:0] Q
);

  D_Flip_Flop #(.trigger("falling")) d_ff_1 (
    .clk(C), .D(D[0]), .Q(Q[0]), .en(Write), .reset(Reset));  // open: Qn, preset
  D_Flip_Flop #(.trigger("falling")) d_ff_2 (
    .clk(C), .D(D[1]), .Q(Q[1]), .en(Write), .reset(Reset));  // open: Qn, preset
  D_Flip_Flop #(.trigger("falling")) d_ff_3 (
    .clk(C), .D(D[2]), .Q(Q[2]), .en(Write), .reset(Reset));  // open: Qn, preset
  D_Flip_Flop #(.trigger("falling")) d_ff_4 (
    .clk(C), .D(D[3]), .Q(Q[3]), .en(Write), .reset(Reset));  // open: Qn, preset
  D_Flip_Flop #(.trigger("falling")) d_ff_5 (
    .clk(C), .D(D[4]), .Q(Q[4]), .en(Write), .reset(Reset));  // open: Qn, preset
  D_Flip_Flop #(.trigger("falling")) d_ff_6 (
    .clk(C), .D(D[5]), .Q(Q[5]), .en(Write), .reset(Reset));  // open: Qn, preset
  D_Flip_Flop #(.trigger("falling")) d_ff_7 (
    .clk(C), .D(D[6]), .Q(Q[6]), .en(Write), .reset(Reset));  // open: Qn, preset
  D_Flip_Flop #(.trigger("falling")) d_ff_8 (
    .clk(C), .D(D[7]), .Q(Q[7]), .en(Write), .reset(Reset));  // open: Qn, preset
  D_Flip_Flop #(.trigger("falling")) d_ff_9 (
    .clk(C), .D(D[8]), .Q(Q[8]), .en(Write), .reset(Reset));  // open: Qn, preset
  D_Flip_Flop #(.trigger("falling")) d_ff_10 (
    .clk(C), .D(D[9]), .Q(Q[9]), .en(Write), .reset(Reset));  // open: Qn, preset
  D_Flip_Flop #(.trigger("falling")) d_ff_11 (
    .clk(C), .D(D[10]), .Q(Q[10]), .en(Write), .reset(Reset));  // open: Qn, preset
  D_Flip_Flop #(.trigger("falling")) d_ff_12 (
    .clk(C), .D(D[11]), .Q(Q[11]), .en(Write), .reset(Reset));  // open: Qn, preset
endmodule

module Register_File (
  input  [2:0] rs,
  input  [2:0] rt,
  input  [2:0] rd,
  input  [11:0] Data,
  input  C,
  input  Reset,
  input  Write
);

  _12_bit_Register r0 (.D(Data), .Reset(Reset), .Write(Write), .C(C));  // open: Q
  _12_bit_Register r1 (.D(Data), .Reset(Reset), .Write(Write), .C(C));  // open: Q
  _12_bit_Register r2 (.D(Data), .Reset(Reset), .Write(Write), .C(C));  // open: Q
  _12_bit_Register r3 (.D(Data), .Reset(Reset), .Write(Write), .C(C));  // open: Q
  _12_bit_Register r4 (.D(Data), .Reset(Reset), .Write(Write), .C(C));  // open: Q
  _12_bit_Register r5 (.D(Data), .Reset(Reset), .Write(Write), .C(C));  // open: Q
  _12_bit_Register r6 (.D(Data), .Reset(Reset), .Write(Write), .C(C));  // open: Q
  _12_bit_Register r7 (.D(Data), .Reset(Reset), .Write(Write), .C(C));  // open: Q
endmodule
